// Logisim project Project.circ as structural Verilog: 8 circuits, main circuit main
module main (
  input  EN,
  input  in_2
);

  wire cdm_8_mark5_1_p2, cdm_8_mark5_1_p3, Clock, controlunit_1_en_2, not_1_out, reset, videochip_1_en_2,
       videochip_2_en_2, videochip_3_en_2;
  wire [1:0] videochip_1_id_2, videochip_2_id_2, videochip_3_id_2;
  wire [3:0] joystick_1_y, joystick_2_y;
  wire [4:0] controlunit_1_ballx, controlunit_1_bally, controlunit_1_leftbaty_2, controlunit_1_rigthbaty,
       videochip_1_ballx_2, videochip_1_bally_2, videochip_1_leftbaty_2, videochip_1_rightbaty_2,
       videochip_2_ballx_2, videochip_2_bally_2, videochip_2_leftbaty_2, videochip_2_rightbaty_2,
       videochip_3_ballx_2, videochip_3_bally_2, videochip_3_leftbaty_2, videochip_3_rightbaty_2;
  wire [7:0] cdm_8_mark5_1_p4, cdm_8_mark5_1_p5, cdm_8_mark5_1_p6, controlled_buffer_2_out, enS, myS;
  wire [31:0] videochip_1_out_8, videochip_1_out_10, videochip_1_out_12, videochip_1_out_15,
       videochip_1_out_17, videochip_1_out_18, videochip_1_out_19, videochip_1_out_20, videochip_2_out_8,
       videochip_2_out_10, videochip_2_out_12, videochip_2_out_15, videochip_2_out_17, videochip_2_out_18,
       videochip_2_out_19, videochip_2_out_20, videochip_3_out_8, videochip_3_out_10, videochip_3_out_12,
       videochip_3_out_15, videochip_3_out_17, videochip_3_out_18, videochip_3_out_19, videochip_3_out_20,
       videochip_4_out_8, videochip_4_out_10, videochip_4_out_12, videochip_4_out_15, videochip_4_out_17,
       videochip_4_out_18, videochip_4_out_19, videochip_4_out_20;

  Clock u_Clock (.out(Clock));
  // CdM_8_mark5 cdm_8_mark5_1: pin names not known; wires that end beside it: Clock, cdm_8_mark5_1_p2, cdm_8_mark5_1_p3, cdm_8_mark5_1_p4, cdm_8_mark5_1_p5, cdm_8_mark5_1_p6
  not not_1 (not_1_out, cdm_8_mark5_1_p3);
  assign cdm_8_mark5_1_p6 = cdm_8_mark5_1_p3 ? controlled_buffer_2_out : 8'bz;  // Controlled_Buffer controlled_buffer_1
  Hex_Digit_Display hex_digit_display_1 (.value(myS[3:0]));  // open: dp
  Joystick joystick_1 (.y(joystick_1_y));  // open: x
  Joystick joystick_2 (.y(joystick_2_y));  // open: x
  assign controlled_buffer_2_out = not_1_out ? cdm_8_mark5_1_p5 : 8'bz;  // Controlled_Buffer controlled_buffer_2
  Hex_Digit_Display hex_digit_display_2 (.value(myS[7:4]));  // open: dp
  DotMatrix #(.matrixcols(32), .matrixrows(32)) dotmatrix_1 (
    .col0(videochip_1_out_8), .col1(videochip_1_out_10), .col2(videochip_1_out_12),
    .col3(videochip_1_out_15), .col4(videochip_1_out_17), .col5(videochip_1_out_18),
    .col6(videochip_1_out_19), .col7(videochip_1_out_20), .col8(videochip_2_out_8),
    .col9(videochip_2_out_10), .col10(videochip_2_out_12), .col11(videochip_2_out_15),
    .col12(videochip_2_out_17), .col13(videochip_2_out_18), .col14(videochip_2_out_19),
    .col15(videochip_2_out_20), .col16(videochip_3_out_8), .col17(videochip_3_out_10),
    .col18(videochip_3_out_12), .col19(videochip_3_out_15), .col20(videochip_3_out_17),
    .col21(videochip_3_out_18), .col22(videochip_3_out_19), .col23(videochip_3_out_20),
    .col24(videochip_4_out_8), .col25(videochip_4_out_10), .col26(videochip_4_out_12),
    .col27(videochip_4_out_15), .col28(videochip_4_out_17), .col29(videochip_4_out_18),
    .col30(videochip_4_out_19), .col31(videochip_4_out_20));
  ControlUnit controlunit_1 (
    .Clock(Clock), .LeftBatY(joystick_1_y), .BallX(controlunit_1_ballx), .BallY(controlunit_1_bally),
    .LeftBatY_2(controlunit_1_leftbaty_2), .EN(EN), .EN_2(controlunit_1_en_2), .RightBatY(joystick_2_y),
    .RigthBatY(controlunit_1_rigthbaty), .EnemyScore(enS), .MyScore(myS), .reset(reset));
  VideoChip videochip_1 (
    .ballY(controlunit_1_bally), .out_8(videochip_1_out_8), .out_10(videochip_1_out_10),
    .out_12(videochip_1_out_12), .out_15(videochip_1_out_15), .out_17(videochip_1_out_17),
    .out_18(videochip_1_out_18), .out_19(videochip_1_out_19), .out_20(videochip_1_out_20),
    .EN(controlunit_1_en_2), .EN_2(videochip_1_en_2), .ballX(controlunit_1_ballx),
    .ballY_2(videochip_1_bally_2), .ballX_2(videochip_1_ballx_2), .ID_2(videochip_1_id_2),
    .LeftBatY(controlunit_1_leftbaty_2), .RightBatY(controlunit_1_rigthbaty),
    .LeftBatY_2(videochip_1_leftbaty_2), .RightBatY_2(videochip_1_rightbaty_2));  // open: ID
  VideoChip videochip_2 (
    .ballY(videochip_1_bally_2), .out_8(videochip_2_out_8), .out_10(videochip_2_out_10),
    .out_12(videochip_2_out_12), .out_15(videochip_2_out_15), .out_17(videochip_2_out_17),
    .out_18(videochip_2_out_18), .out_19(videochip_2_out_19), .out_20(videochip_2_out_20),
    .EN(videochip_1_en_2), .EN_2(videochip_2_en_2), .ballX(videochip_1_ballx_2),
    .ballY_2(videochip_2_bally_2), .ballX_2(videochip_2_ballx_2), .ID_2(videochip_2_id_2),
    .LeftBatY(videochip_1_leftbaty_2), .RightBatY(videochip_1_rightbaty_2),
    .LeftBatY_2(videochip_2_leftbaty_2), .RightBatY_2(videochip_2_rightbaty_2), .ID(videochip_1_id_2));
  RAM ram_1 (
    .addr(cdm_8_mark5_1_p4), .data(controlled_buffer_2_out), .sel(cdm_8_mark5_1_p2), .clk(Clock),
    .ld(cdm_8_mark5_1_p3));  // open: clr
  VideoChip videochip_3 (
    .ballY(videochip_2_bally_2), .out_8(videochip_3_out_8), .out_10(videochip_3_out_10),
    .out_12(videochip_3_out_12), .out_15(videochip_3_out_15), .out_17(videochip_3_out_17),
    .out_18(videochip_3_out_18), .out_19(videochip_3_out_19), .out_20(videochip_3_out_20),
    .EN(videochip_2_en_2), .EN_2(videochip_3_en_2), .ballX(videochip_2_ballx_2),
    .ballY_2(videochip_3_bally_2), .ballX_2(videochip_3_ballx_2), .ID_2(videochip_3_id_2),
    .LeftBatY(videochip_2_leftbaty_2), .RightBatY(videochip_2_rightbaty_2),
    .LeftBatY_2(videochip_3_leftbaty_2), .RightBatY_2(videochip_3_rightbaty_2), .ID(videochip_2_id_2));
  Hex_Digit_Display hex_digit_display_3 (.value(enS[3:0]));  // open: dp
  VideoChip videochip_4 (
    .ballY(videochip_3_bally_2), .out_8(videochip_4_out_8), .out_10(videochip_4_out_10),
    .out_12(videochip_4_out_12), .out_15(videochip_4_out_15), .out_17(videochip_4_out_17),
    .out_18(videochip_4_out_18), .out_19(videochip_4_out_19), .out_20(videochip_4_out_20),
    .EN(videochip_3_en_2), .ballX(videochip_3_ballx_2), .LeftBatY(videochip_3_leftbaty_2),
    .RightBatY(videochip_3_rightbaty_2), .ID(videochip_3_id_2));  // open: EN_2, ballY_2, ballX_2, ID_2, LeftBatY_2, RightBatY_2
  Hex_Digit_Display hex_digit_display_4 (.value(enS[7:4]));  // open: dp
  Button R (.out(reset));

  // Notes on the sheet:
  //   Click to reset the game
endmodule

module ControlUnit (
  input  EN,
  input  Clock,
  input  [3:0] LeftBatY,
  input  [3:0] RightBatY,
  input  reset,
  output EN_2,
  output [7:0] EnemyScore,
  output [7:0] MyScore,
  output [4:0] RigthBatY,
  output [4:0] LeftBatY_2,
  output [4:0] BallX,
  output [4:0] BallY
);

  wire and_1_out, and_2_out, and_3_out, and_4_out, and_5_out, and_6_out, buffer_1_out, comparator_1_eq,
       comparator_2_eq, comparator_3_eq, comparator_4_eq, comparator_5_eq, comparator_6_eq, comparator_7_gt,
       comparator_8_eq, comparator_9_gt, comparator_10_eq, d_ff_1_q, d_ff_1_qn, d_ff_2_q, d_ff_2_qn, EN_t,
       or_2_out, or_3_out, X_q, X_qn, Y_q, Y_qn;
  wire [4:0] adder_1_out, adder_2_out, multiplexer_1_out, multiplexer_2_out, subtractor_1_out,
       subtractor_2_out;
  wire [5:0] bitadder_1_out, bitadder_2_out, bitadder_3_out, bitadder_4_out;
  wire [31:0] bat_1_out_2, bat_2_out_2, decoder_1_out0, decoder_2_out0, xor_1_out, xor_2_out;

  or or_1 (EN_t, reset, ~EN);  // OR_Gate
  Subtractor #(.width(5)) subtractor_1 (.a(BallX), .b(5'b00001), .out(subtractor_1_out));  // open: bin, bout
  Adder #(.width(5)) adder_1 (.a(BallX), .b(5'b00001), .out(adder_1_out));  // open: cin, cout
  Subtractor #(.width(5)) subtractor_2 (.a(BallY), .b(5'b00001), .out(subtractor_2_out));  // open: bin, bout
  Adder #(.width(5)) adder_2 (.a(BallY), .b(5'b00001), .out(adder_2_out));  // open: cin, cout
  buf buffer_1 (buffer_1_out, and_1_out);
  D_Flip_Flop X (.clk(or_2_out), .D(X_qn), .Q(X_q), .Qn(X_qn), .preset(EN_t));  // open: en, reset
  D_Flip_Flop d_ff_1 (.clk(d_ff_2_q), .D(d_ff_1_qn), .Q(d_ff_1_q), .Qn(d_ff_1_qn));  // open: preset, en, reset
  D_Flip_Flop d_ff_2 (.clk(Clock), .D(d_ff_2_qn), .Q(d_ff_2_q), .Qn(d_ff_2_qn));  // open: preset, en, reset
  LeftBatMovement leftbatmovement_1 (.EN(EN_t), .Clock(Clock), .LeftBatY(LeftBatY), .LeftBatYFin(LeftBatY_2));
  Counter #(.width(5), .max('h1f)) BatY (
    .load(and_1_out), .Q(RigthBatY), .clk(buffer_1_out), .clr(EN_t));  // open: D, count, carry
  Pull_Resistor pull_resistor_1 (.node(buffer_1_out));
  buf buffer_2 (buffer_1_out, and_2_out);
  and and_1 (and_1_out, RightBatY[0], RightBatY[1], RightBatY[2], RightBatY[3], Clock);
  and and_2 (and_2_out, ~RightBatY[3], ~RightBatY[2], ~RightBatY[1], RightBatY[0], Clock);  // AND_Gate
  D_Flip_Flop Y (.clk(or_3_out), .D(Y_qn), .Q(Y_q), .Qn(Y_qn), .preset(EN_t));  // open: en, reset
  Register #(.width(5)) u_ballX (.D(multiplexer_1_out), .Q(BallX), .clk(d_ff_1_q), .clr(EN_t));  // open: en
  Multiplexer #(.width(5), .enable("false")) multiplexer_1 (
    .in0(subtractor_1_out), .in1(adder_1_out), .out(multiplexer_1_out), .sel(X_q));
  Multiplexer #(.width(5), .enable("false")) multiplexer_2 (
    .in0(subtractor_2_out), .in1(adder_2_out), .out(multiplexer_2_out), .sel(Y_q));
  Register #(.width(5)) u_ballY (.D(multiplexer_2_out), .Q(BallY), .clk(d_ff_1_q), .clr(EN_t));  // open: en
  Comparator #(.width(5), .mode("unsigned")) comparator_1 (
    .a({5{1'b1}}), .b(BallY), .eq(comparator_1_eq));  // open: gt, lt
  Comparator #(.width(5), .mode("unsigned")) comparator_2 (
    .a({5{1'b0}}), .b(BallY), .eq(comparator_2_eq));  // open: gt, lt
  Decoder #(.select(5), .disabled(0), .enable("false")) decoder_1 (
    .out0(decoder_1_out0[0]), .out1(decoder_1_out0[1]), .out2(decoder_1_out0[2]), .out3(decoder_1_out0[3]),
    .out4(decoder_1_out0[4]), .out5(decoder_1_out0[5]), .out6(decoder_1_out0[6]), .out7(decoder_1_out0[7]),
    .out8(decoder_1_out0[8]), .out9(decoder_1_out0[9]), .out10(decoder_1_out0[10]),
    .out11(decoder_1_out0[11]), .out12(decoder_1_out0[12]), .out13(decoder_1_out0[13]),
    .out14(decoder_1_out0[14]), .out15(decoder_1_out0[15]), .out16(decoder_1_out0[16]),
    .out17(decoder_1_out0[17]), .out18(decoder_1_out0[18]), .out19(decoder_1_out0[19]),
    .out20(decoder_1_out0[20]), .out21(decoder_1_out0[21]), .out22(decoder_1_out0[22]),
    .out23(decoder_1_out0[23]), .out24(decoder_1_out0[24]), .out25(decoder_1_out0[25]),
    .out26(decoder_1_out0[26]), .out27(decoder_1_out0[27]), .out28(decoder_1_out0[28]),
    .out29(decoder_1_out0[29]), .out30(decoder_1_out0[30]), .out31(decoder_1_out0[31]),
    .sel(multiplexer_2_out));
  Comparator #(.width(5), .mode("unsigned")) comparator_3 (
    .a({5{1'b1}}), .b(BallX), .eq(comparator_3_eq));  // open: gt, lt
  or or_2 (or_2_out, comparator_3_eq, comparator_4_eq, and_5_out, and_6_out);
  Comparator #(.width(5), .mode("unsigned")) comparator_4 (
    .a({5{1'b0}}), .b(BallX), .eq(comparator_4_eq));  // open: gt, lt
  or or_3 (or_3_out, comparator_1_eq, comparator_2_eq);
  Decoder #(.select(5), .disabled(0), .enable("false")) decoder_2 (
    .out0(decoder_2_out0[0]), .out1(decoder_2_out0[1]), .out2(decoder_2_out0[2]), .out3(decoder_2_out0[3]),
    .out4(decoder_2_out0[4]), .out5(decoder_2_out0[5]), .out6(decoder_2_out0[6]), .out7(decoder_2_out0[7]),
    .out8(decoder_2_out0[8]), .out9(decoder_2_out0[9]), .out10(decoder_2_out0[10]),
    .out11(decoder_2_out0[11]), .out12(decoder_2_out0[12]), .out13(decoder_2_out0[13]),
    .out14(decoder_2_out0[14]), .out15(decoder_2_out0[15]), .out16(decoder_2_out0[16]),
    .out17(decoder_2_out0[17]), .out18(decoder_2_out0[18]), .out19(decoder_2_out0[19]),
    .out20(decoder_2_out0[20]), .out21(decoder_2_out0[21]), .out22(decoder_2_out0[22]),
    .out23(decoder_2_out0[23]), .out24(decoder_2_out0[24]), .out25(decoder_2_out0[25]),
    .out26(decoder_2_out0[26]), .out27(decoder_2_out0[27]), .out28(decoder_2_out0[28]),
    .out29(decoder_2_out0[29]), .out30(decoder_2_out0[30]), .out31(decoder_2_out0[31]),
    .sel(multiplexer_1_out));
  Bat bat_1 (.BatY(LeftBatY_2), .out_2(bat_1_out_2));
  Bat bat_2 (.BatY(RigthBatY), .out_2(bat_2_out_2));
  assign xor_1_out = bat_1_out_2 ^ decoder_1_out0;  // XOR_Gate xor_1, 32 bits wide
  Comparator #(.width(5), .mode("unsigned")) comparator_5 (
    .a({5{1'b0}}), .b(BallX), .eq(comparator_5_eq));  // open: gt, lt
  Comparator #(.width(5), .mode("unsigned")) comparator_6 (
    .a({5{1'b1}}), .b(BallX), .eq(comparator_6_eq));  // open: gt, lt
  BitAdder #(.width(32)) bitadder_1 (.in0(bat_1_out_2), .out(bitadder_1_out));
  BitAdder #(.width(32)) bitadder_2 (.in0(xor_1_out), .out(bitadder_2_out));
  assign xor_2_out = bat_2_out_2 ^ decoder_1_out0;  // XOR_Gate xor_2, 32 bits wide
  and and_3 (and_3_out, ~X_q, comparator_5_eq);  // AND_Gate
  and and_4 (and_4_out, X_q, comparator_6_eq);
  Comparator #(.width(6), .mode("unsigned")) comparator_7 (
    .a(bitadder_1_out), .b(bitadder_2_out), .gt(comparator_7_gt));  // open: eq, lt
  and and_5 (and_5_out, comparator_7_gt, comparator_8_eq);
  Comparator #(.width(32), .mode("unsigned")) comparator_8 (
    .a(decoder_2_out0), .b(32'h8), .eq(comparator_8_eq));  // open: gt, lt
  BitAdder #(.width(32)) bitadder_3 (.in0(bat_2_out_2), .out(bitadder_3_out));
  Comparator #(.width(6), .mode("unsigned")) comparator_9 (
    .a(bitadder_3_out), .b(bitadder_4_out), .gt(comparator_9_gt));  // open: eq, lt
  BitAdder #(.width(32)) bitadder_4 (.in0(xor_2_out), .out(bitadder_4_out));
  Comparator #(.width(32), .mode("unsigned")) comparator_10 (
    .a(decoder_2_out0), .b(32'h10000000), .eq(comparator_10_eq));  // open: gt, lt
  and and_6 (and_6_out, comparator_9_gt, comparator_10_eq);
  ScoreCounter scorecounter_1 (.Score(EnemyScore), .flag(and_3_out), .reset(EN_t));
  ScoreCounter scorecounter_2 (.Score(MyScore), .flag(and_4_out), .reset(EN_t));

  assign EN_2 = EN;

  // Other names for the same wires on the sheet: EN_In = EN; LeftBatYFin[4:0] = LeftBatY_2;
  //   RightBatYFin[4:0] = RigthBatY; RigthBatY_t[3:0] = RightBatY

  // Notes on the sheet:
  //   buffer_1 drives only 1 and floats otherwise
  //   buffer_2 drives only 1 and floats otherwise
endmodule

module VideoChip (
  input  EN,
  input  [4:0] ballX,
  input  [4:0] ballY,
  input  [1:0] ID,
  input  [4:0] LeftBatY,
  input  [4:0] RightBatY,
  output EN_2,
  output [31:0] out_8,
  output [4:0] ballY_2,
  output [31:0] out_10,
  output [4:0] ballX_2,
  output [31:0] out_12,
  output [1:0] ID_2,
  output [4:0] LeftBatY_2,
  output [31:0] out_15,
  output [4:0] RightBatY_2,
  output [31:0] out_17,
  output [31:0] out_18,
  output [31:0] out_19,
  output [31:0] out_20
);

  wire comparator_1_eq;
  wire [31:0] demultiplexer_1_out0, FinalCol3, FinalCol4, LbcRes, RbcRes;

  Pull_Resistor pull_resistor_1 (.node(EN));
  Pull_Resistor pull_resistor_2 (.node(ballX));
  Pull_Resistor pull_resistor_3 (.node(ballY));
  Pull_Resistor pull_resistor_4 (.node(ID));
  Pull_Resistor pull_resistor_5 (.node(LeftBatY));
  Pull_Resistor pull_resistor_6 (.node(RightBatY));
  Demultiplexer #(.select(5), .enable("false")) demultiplexer_1 (
    .out0(demultiplexer_1_out0[0]), .out1(demultiplexer_1_out0[1]), .out2(demultiplexer_1_out0[2]),
    .out3(demultiplexer_1_out0[3]), .out4(demultiplexer_1_out0[4]), .out5(demultiplexer_1_out0[5]),
    .out6(demultiplexer_1_out0[6]), .out7(demultiplexer_1_out0[7]), .out8(demultiplexer_1_out0[8]),
    .out9(demultiplexer_1_out0[9]), .out10(demultiplexer_1_out0[10]), .out11(demultiplexer_1_out0[11]),
    .out12(demultiplexer_1_out0[12]), .out13(demultiplexer_1_out0[13]), .out14(demultiplexer_1_out0[14]),
    .out15(demultiplexer_1_out0[15]), .out16(demultiplexer_1_out0[16]), .out17(demultiplexer_1_out0[17]),
    .out18(demultiplexer_1_out0[18]), .out19(demultiplexer_1_out0[19]), .out20(demultiplexer_1_out0[20]),
    .out21(demultiplexer_1_out0[21]), .out22(demultiplexer_1_out0[22]), .out23(demultiplexer_1_out0[23]),
    .out24(demultiplexer_1_out0[24]), .out25(demultiplexer_1_out0[25]), .out26(demultiplexer_1_out0[26]),
    .out27(demultiplexer_1_out0[27]), .out28(demultiplexer_1_out0[28]), .out29(demultiplexer_1_out0[29]),
    .out30(demultiplexer_1_out0[30]), .out31(demultiplexer_1_out0[31]), .in(EN), .sel(ballY));
  LeftBatConstructor leftbatconstructor_1 (.ID(ID), .out_3(LbcRes), .LeftBatY(LeftBatY));
  RightBatConstructor rightbatconstructor_1 (.RigthBatY(RightBatY), .ID(ID), .out_3(RbcRes));
  Demultiplexer #(.select(3), .width(32), .disabled(0)) demultiplexer_2 (
    .out0(out_8), .out1(out_10), .out2(out_12), .out3(FinalCol3), .out4(FinalCol4), .out5(out_18),
    .out6(out_19), .out7(out_20), .in(demultiplexer_1_out0), .sel(ballX[2:0]), .en(comparator_1_eq));
  Comparator #(.width(2), .mode("unsigned")) comparator_1 (
    .a(ballX[4:3]), .b(ID), .eq(comparator_1_eq));  // open: gt, lt
  assign out_15 = FinalCol3 | LbcRes;  // OR_Gate or_1, 32 bits wide
  assign out_17 = FinalCol4 | RbcRes;  // OR_Gate or_2, 32 bits wide
  Adder #(.width(2)) adder_1 (.a(ID), .b(2'b01), .out(ID_2));  // open: cin, cout

  assign ballX_2 = ballX;
  assign ballY_2 = ballY;
  assign EN_2 = EN;
  assign LeftBatY_2 = LeftBatY;
  assign RightBatY_2 = RightBatY;

  // Other names for the same wires on the sheet: FinalCol0[31:0] = out_8; FinalCol1[31:0] = out_10;
  //   FinalCol2[31:0] = out_12; FinalCol5[31:0] = out_18; FinalCol6[31:0] = out_19; FinalCol7[31:0] = out_20
endmodule

// LBC
module LeftBatConstructor (
  input  [1:0] ID,
  input  [4:0] LeftBatY,
  output [31:0] out_3
);

  wire comparator_1_eq;
  wire [31:0] bat_1_out_2;

  Comparator #(.width(2)) comparator_1 (.a(ID), .b(2'b00), .eq(comparator_1_eq));  // open: gt, lt
  assign out_3 = comparator_1_eq ? bat_1_out_2 : 32'bz;  // Controlled_Buffer controlled_buffer_1
  Bat bat_1 (.BatY(LeftBatY), .out_2(bat_1_out_2));
  Pull_Resistor pull_resistor_1 (.node(out_3));
endmodule

// RBC
module RightBatConstructor (
  input  [1:0] ID,
  input  [4:0] RigthBatY,
  output [31:0] out_3
);

  wire comparator_1_eq;
  wire [31:0] bat_1_out_2;

  Comparator #(.width(2)) comparator_1 (.a(ID), .b(2'b11), .eq(comparator_1_eq));  // open: gt, lt
  Bat bat_1 (.BatY(RigthBatY), .out_2(bat_1_out_2));
  Pull_Resistor pull_resistor_1 (.node(out_3));
  assign out_3 = comparator_1_eq ? bat_1_out_2 : 32'bz;  // Controlled_Buffer controlled_buffer_1
endmodule

module Bat (
  input  [4:0] BatY,
  output [31:0] out_2
);

  wire [0:0] pull_resistor_2_node;
  wire [31:0] decoder_1_out31;
  wire [31:31] pull_resistor_1_node;

  Decoder #(.select(5), .disabled(0), .enable("false")) decoder_1 (
    .out0(decoder_1_out31[0]), .out1(decoder_1_out31[1]), .out2(decoder_1_out31[2]),
    .out3(decoder_1_out31[3]), .out4(decoder_1_out31[4]), .out5(decoder_1_out31[5]),
    .out6(decoder_1_out31[6]), .out7(decoder_1_out31[7]), .out8(decoder_1_out31[8]),
    .out9(decoder_1_out31[9]), .out10(decoder_1_out31[10]), .out11(decoder_1_out31[11]),
    .out12(decoder_1_out31[12]), .out13(decoder_1_out31[13]), .out14(decoder_1_out31[14]),
    .out15(decoder_1_out31[15]), .out16(decoder_1_out31[16]), .out17(decoder_1_out31[17]),
    .out18(decoder_1_out31[18]), .out19(decoder_1_out31[19]), .out20(decoder_1_out31[20]),
    .out21(decoder_1_out31[21]), .out22(decoder_1_out31[22]), .out23(decoder_1_out31[23]),
    .out24(decoder_1_out31[24]), .out25(decoder_1_out31[25]), .out26(decoder_1_out31[26]),
    .out27(decoder_1_out31[27]), .out28(decoder_1_out31[28]), .out29(decoder_1_out31[29]),
    .out30(decoder_1_out31[30]), .out31(decoder_1_out31[31]), .sel(BatY));
  Pull_Resistor pull_resistor_1 (.node(pull_resistor_1_node[31]));
  Pull_Resistor pull_resistor_2 (.node(pull_resistor_2_node[0]));
  assign out_2 = {pull_resistor_1_node[31], decoder_1_out31[31:1]} | decoder_1_out31 | {decoder_1_out31[30:0], pull_resistor_2_node[0]};  // OR_Gate or_1, 32 bits wide
endmodule

module ScoreCounter (
  input  flag,
  input  reset,
  output [7:0] Score
);

  wire [7:0] counter_1_q;
  wire [7:4] divider_1_out, divider_1_rem;

  Counter #(.max('h63)) counter_1 (.Q(counter_1_q), .clk(flag), .clr(reset));  // open: load, D, count, carry
  Divider divider_1 (
    .a(counter_1_q), .b(8'ha), .out({divider_1_out, Score[3:0]}), .rem({divider_1_rem, Score[7:4]}));  // open: upper
endmodule

// LBM
module LeftBatMovement (
  input  EN,
  input  Clock,
  input  [3:0] LeftBatY,
  output [4:0] LeftBatYFin
);

  wire and_1_out, and_2_out, comparator_1_eq, pull_resistor_3_node;
  wire [2:0] pull_resistor_1_node;
  wire [4:0] adder_1_out, multiplexer_1_out, subtractor_1_out;

  Adder #(.width(5)) adder_1 (.a(LeftBatYFin), .b(5'b00001), .out(adder_1_out));  // open: cin, cout
  Subtractor #(.width(5)) subtractor_1 (.a(LeftBatYFin), .b(5'b00001), .out(subtractor_1_out));  // open: bin, bout
  Pull_Resistor pull_resistor_1 (.node(pull_resistor_1_node));
  Priority_Encoder #(.disabled(0)) priority_encoder_1 (
    .in1(and_2_out), .in2(and_1_out), .in3(comparator_1_eq), .in4(pull_resistor_3_node),
    .out(pull_resistor_1_node));  // open: in0, in5, in6, in7, en_in, gs, en_out
  Multiplexer #(.select(3), .width(5), .enable("false")) multiplexer_1 (
    .in0(LeftBatYFin), .in1(adder_1_out), .in2(subtractor_1_out), .in3(5'b11101), .in4(5'b00001),
    .out(multiplexer_1_out), .sel(pull_resistor_1_node));  // open: in5, in6, in7
  and and_1 (and_1_out, LeftBatY[0], LeftBatY[1], LeftBatY[2], LeftBatY[3]);
  and and_2 (and_2_out, ~LeftBatY[3], ~LeftBatY[2], ~LeftBatY[1], LeftBatY[0]);  // AND_Gate
  Register #(.width(5)) register_1 (.D(multiplexer_1_out), .Q(LeftBatYFin), .clk(Clock), .clr(EN));  // open: en
  Comparator #(.width(5), .mode("unsigned")) comparator_1 (
    .a(adder_1_out), .b({5{1'b0}}), .eq(comparator_1_eq));  // open: gt, lt
  Pull_Resistor pull_resistor_2 (.node(comparator_1_eq));
  Pull_Resistor pull_resistor_3 (.node(pull_resistor_3_node));
  Comparator #(.width(5), .mode("unsigned")) comparator_2 (
    .a(subtractor_1_out), .b({5{1'b1}}), .eq(pull_resistor_3_node));  // open: gt, lt
endmodule
